# Fritzing sketch prod-circuit (saved by Fritzing 0.8.7b)
perfboards: 1

parts:
  U1 = 74HC595 [package="DIP16 [THT]"]
  IC1 = ULN2003A [package="DIP16 [THT]"]  # not connected
  U2 = 74HC595 [package="DIP16 [THT]"]
  U3 = 74HC595 [package="DIP16 [THT]"]
  R1 = Resistor [tolerance=±5% resistance=220 package=THT]  # not connected
  R2 = Resistor [tolerance=±5% resistance=220 package=THT]  # not connected
  R3 = Resistor [tolerance=±5% resistance=220 package=THT]  # not connected
  R4 = Resistor [tolerance=±5% resistance=220 package=THT]  # not connected
  R5 = Resistor [tolerance=±5% resistance=220 package=THT]  # not connected
  R6 = Resistor [tolerance=±5% resistance=220 package=THT]  # not connected
  R8 = Resistor [tolerance=±5% resistance=220 package=THT]  # not connected
  R10 = Resistor [tolerance=±5% resistance=220 package=THT]  # not connected
  R11 = Resistor [tolerance=±5% resistance=220 package=THT]  # not connected
  R12 = Resistor [tolerance=±5% resistance=220 package=THT]  # not connected
  R13 = Resistor [tolerance=±5% resistance=220 package=THT]  # not connected
  R14 = Resistor [tolerance=±5% resistance=220 package=THT]  # not connected
  R15 = Resistor [tolerance=±5% resistance=220 package=THT]  # not connected
  R16 = Resistor [tolerance=±5% resistance=220 package=THT]  # not connected
  R17 = Resistor [tolerance=±5% resistance=220 package=THT]  # not connected
  R18 = Resistor [tolerance=±5% resistance=220 package=THT]  # not connected
  R20 = Resistor [tolerance=±5% resistance=220 package=THT]  # not connected
  R21 = Resistor [tolerance=±5% resistance=220 package=THT]  # not connected
  R22 = Resistor [tolerance=±5% resistance=220 package=THT]  # not connected
  R23 = Resistor [tolerance=±5% resistance=220 package=THT]  # not connected
  R24 = Resistor [tolerance=±5% resistance=220 package=THT]  # not connected
  R25 = Resistor [tolerance=±5% resistance=220 package=THT]  # not connected
  R26 = Resistor [tolerance=±5% resistance=220 package=THT]  # not connected
  R27 = Resistor [tolerance=±5% resistance=220 package=THT]  # not connected
  J1 = male pin header, 8 pins [form="♂ (male)"]  # not connected
  J2 = male pin header, 8 pins [form="♂ (male)"]  # not connected
  J3 = male pin header, 8 pins [form="♂ (male)"]  # not connected
  U4 = atmega328 [package=dip]  # not connected
  U5 = Voltage Regulator - 5V [package="TO220 [THT]"]  # not connected
  Power_plug1 = Power plug  # not connected
  J4 = male pin header, 8 pins [form="♂ (male)"]  # not connected
  J5 = male pin header, 8 pins [form="♂ (male)"]  # not connected
  J6 = male pin header, 8 pins [form="♂ (male)"]  # not connected
  XTAL1 = Crystal [frequency="16 Mhz" package=THT]  # not connected
  C1 = Electrolytic Capacitor [capacitance=1µF package="100 mil [THT, electrolytic]"]  # not connected
  Q1 = PNP-Transistor [package="TO92 [THT]"]  # not connected
  R29 = Resistor [tolerance=±5% resistance=220 package=THT]  # not connected
  J7 = male pin header, 3 pins [form="♂ (male)"]  # not connected
  R30 = Resistor [tolerance=±5% resistance=220 package=THT]  # not connected

nets:
  N1: U1.Q7', U2.DS
  N2: U1.SH_CP, U2.SH_CP, U3.SH_CP
  N3: U1.ST_CP, U2.ST_CP, U3.ST_CP
  N4: U2.Q7', U3.DS
