# Fritzing sketch schematic (saved by Fritzing 1.0.0d)
breadboards: 1

parts:
  U5 = atmega328 [package=dip]
  7805_regulator = Voltage Regulator - 5V [package="TO220 [THT]"]
  R31 = Resistor [tolerance=±5% resistance=10k power=0.25W package=THT]
  XTAL2 = Crystal [frequency="16 Mhz" package=THT]
  22_pF = Ceramic Capacitor [capacitance=0.22mF package="100 mil [THT, multilayer]"]
  22_pF1 = Ceramic Capacitor [capacitance=0.22mF package="100 mil [THT, multilayer]"]
  ULN2803 = IC, DIP package, 18 pins [chip_label=IC]
  Led_Rows = Header 8 [package=1x08_smd]
  U6 = 74HC595 [package="DIP16 [THT]"]
  R32 = Resistor [tolerance=±5% resistance=220 power=0.25W package=THT]
  R33 = Resistor [tolerance=±5% resistance=220 power=0.25W package=THT]
  R34 = Resistor [tolerance=±5% resistance=220 power=0.25W package=THT]
  R35 = Resistor [tolerance=±5% resistance=220 power=0.25W package=THT]
  R36 = Resistor [tolerance=±5% resistance=220 power=0.25W package=THT]
  R37 = Resistor [tolerance=±5% resistance=220 power=0.25W package=THT]
  R38 = Resistor [tolerance=±5% resistance=220 power=0.25W package=THT]
  R39 = Resistor [tolerance=±5% resistance=220 power=0.25W package=THT]
  Led_Columns1 = Header 8 [package=1x08_smd]
  U7 = 74HC595 [package="DIP16 [THT]"]
  U8 = 74HC595 [package="DIP16 [THT]"]
  Led_Columns2 = Header 8 [package=1x08_smd]
  R40 = Resistor [tolerance=±5% resistance=220 power=0.25W package=THT]
  R41 = Resistor [tolerance=±5% resistance=220 power=0.25W package=THT]
  R42 = Resistor [tolerance=±5% resistance=220 power=0.25W package=THT]
  R43 = Resistor [tolerance=±5% resistance=220 power=0.25W package=THT]
  R44 = Resistor [tolerance=±5% resistance=220 power=0.25W package=THT]
  R45 = Resistor [tolerance=±5% resistance=220 power=0.25W package=THT]
  R46 = Resistor [tolerance=±5% resistance=220 power=0.25W package=THT]
  R47 = Resistor [tolerance=±5% resistance=220 power=0.25W package=THT]
  Led_Columns3 = Header 8 [package=1x08_smd]
  R48 = Resistor [tolerance=±5% resistance=220 power=0.25W package=THT]
  R49 = Resistor [tolerance=±5% resistance=220 power=0.25W package=THT]
  R50 = Resistor [tolerance=±5% resistance=220 power=0.25W package=THT]
  R51 = Resistor [tolerance=±5% resistance=220 power=0.25W package=THT]
  R52 = Resistor [tolerance=±5% resistance=220 power=0.25W package=THT]
  R53 = Resistor [tolerance=±5% resistance=220 power=0.25W package=THT]
  R54 = Resistor [tolerance=±5% resistance=220 power=0.25W package=THT]
  R55 = Resistor [tolerance=±5% resistance=220 power=0.25W package=THT]

nets:
  N1: U5.RESET, R31.Pin_1
  N2: U5.D0_(RX), ULN2803.pin1
  N3: U5.D1_(TX), ULN2803.pin2
  N4: U5.D2, ULN2803.pin3
  N5: U5.D3_(PWM), ULN2803.pin4
  N6: U5.D4, ULN2803.pin5
  VCC: U5.VCC, U5.AVCC, U5.AREF, 7805_regulator.output_voltage, R31.Pin_0, ULN2803.pin10, U6.MR, U7.MR, U7.VCC, U8.MR, U8.VCC
  GND: U5.GND, 7805_regulator.GND, 22_pF.1, 22_pF1.1, ULN2803.pin9, U6.GND, U6.OE, U7.GND, U7.OE, U8.GND, U8.OE
  N7: U5.XLAT1, XTAL2.pin_0, 22_pF.0
  N8: U5.XLAT2, XTAL2.pin_1, 22_pF1.0
  N9: U5.D5_(PWM), ULN2803.pin6
  N10: U5.D6_(PWM), ULN2803.pin7
  N11: U5.D7, ULN2803.pin8
  N12: U5.D8, U6.ST_CP, U7.ST_CP, U8.ST_CP
  N13: U5.D11_(PWM), U6.DS
  N14: U5.D12, U6.SH_CP, U7.SH_CP, U8.SH_CP
  5V: 7805_regulator.input_voltage
  N15: ULN2803.pin11, Led_Rows.8
  N16: ULN2803.pin12, Led_Rows.7
  N17: ULN2803.pin13, Led_Rows.6
  N18: ULN2803.pin14, Led_Rows.5
  N19: ULN2803.pin15, Led_Rows.4
  N20: ULN2803.pin16, Led_Rows.3
  N21: ULN2803.pin17, Led_Rows.2
  N22: ULN2803.pin18, Led_Rows.1
  N23: U6.Q1, R33.Pin_0
  N24: U6.Q2, R34.Pin_0
  N25: U6.Q3, R35.Pin_0
  N26: U6.Q4, R36.Pin_0
  N27: U6.Q5, R37.Pin_0
  N28: U6.Q6, R38.Pin_0
  N29: U6.Q7, R39.Pin_0
  N30: U6.Q7', U7.DS
  N31: U6.Q0, R32.Pin_0
  N32: R32.Pin_1, Led_Columns1.1
  N33: R33.Pin_1, Led_Columns1.2
  N34: R34.Pin_1, Led_Columns1.3
  N35: R35.Pin_1, Led_Columns1.4
  N36: R36.Pin_1, Led_Columns1.5
  N37: R37.Pin_1, Led_Columns1.6
  N38: R38.Pin_1, Led_Columns1.7
  N39: R39.Pin_1, Led_Columns1.8
  N40: U7.Q1, R47.Pin_0
  N41: U7.Q2, R46.Pin_0
  N42: U7.Q3, R43.Pin_0
  N43: U7.Q4, R41.Pin_0
  N44: U7.Q5, R45.Pin_0
  N45: U7.Q6, R40.Pin_0
  N46: U7.Q7, R42.Pin_0
  N47: U7.Q7', U8.DS
  N48: U7.Q0, R44.Pin_0
  N49: U8.Q1, R55.Pin_0
  N50: U8.Q2, R49.Pin_0
  N51: U8.Q3, R54.Pin_0
  N52: U8.Q4, R48.Pin_0
  N53: U8.Q5, R50.Pin_0
  N54: U8.Q6, R52.Pin_0
  N55: U8.Q7, R53.Pin_0
  N56: U8.Q0, R51.Pin_0
  N57: Led_Columns2.1, R44.Pin_1
  N58: Led_Columns2.2, R47.Pin_1
  N59: Led_Columns2.3, R46.Pin_1
  N60: Led_Columns2.4, R43.Pin_1
  N61: Led_Columns2.5, R41.Pin_1
  N62: Led_Columns2.6, R45.Pin_1
  N63: Led_Columns2.7, R40.Pin_1
  N64: Led_Columns2.8, R42.Pin_1
  N65: Led_Columns3.1, R51.Pin_1
  N66: Led_Columns3.2, R55.Pin_1
  N67: Led_Columns3.3, R49.Pin_1
  N68: Led_Columns3.4, R54.Pin_1
  N69: Led_Columns3.5, R48.Pin_1
  N70: Led_Columns3.6, R50.Pin_1
  N71: Led_Columns3.7, R52.Pin_1
  N72: Led_Columns3.8, R53.Pin_1
